# Fritzing sketch PIR_buzzer_led (saved by Fritzing 0.9.0b)
circuit board: 8.46667cm x 5.64444cm
breadboards: 1

parts:
  Composant1 = Arduino Uno (Rev3)
  PIR1 = PIR sensor
  R1 = Resistor [tolerance=±5% resistance=220 package=THT]
  LED1 = LED - 5mm [color="Red (633nm)" package="5 mm [THT]"]
  J1 = Piezo Speaker

nets:
  N1: Composant1.D10_PWM/SS, J1.pin2
  N2: Composant1.D13/SCK, R1.Pin_1
  N3: Composant1.D2, PIR1.SIG
  5V: Composant1.5V, PIR1.VDD
  GND: Composant1.GND, PIR1.GND, LED1.cathode, J1.pin1
  N4: R1.Pin_0, LED1.anode
