# Fritzing sketch NodeMcu_PIR_buzzer_led (saved by Fritzing 0.8.5b)
circuit board: 8.46667cm x 5.64444cm
breadboards: 1

parts:
  U1 = NodeMCU V1.0
  PIR1 = PIR sensor
  J1 = Piezo Speaker
  LED1 = LED - 5mm [color="Red (633nm)" package="5 mm [THT]"]
  Power_plug1 = Power plug
  R1 = Resistor [tolerance=±5% resistance=220 package=THT]

nets:
  N1: U1.D2, J1.pin2
  N2: U1.D3, R1.Pin_1
  N3: U1.D4, PIR1.SIG
  GND: U1.GND, PIR1.GND, J1.pin1, LED1.cathode, Power_plug1.GND
  VIN: U1.Vin, PIR1.VDD, Power_plug1.VCC
  N4: LED1.anode, R1.Pin_0

custom parts:
  NodeMCU V1.0: ESP8266 based NodeMCU
